// Logisim project DSD_CS23B1039.circ as structural Verilog: 1 circuit, main circuit main
module main (
  input  [3:0] x,
  input  [3:0] y,
  input  C0,
  input  in_4
);

  wire and_1_out, C1_out, C2_out, C3_out, G0_out, G1_out, G2_out, G3_out, P0_out, P1_out, P1G0_out,
       P1P0C0_out, P2_out, P2G1_out, P2P1G0_out, P2P1P0C0_out, P3_out, P3G2_out, P3P2G1_out, P3P2P1G0_out,
       P3P2P1P0C0_out;
  wire [0:0] C4_out;
  wire [3:0] S0_out;

  and P2G1 (P2G1_out, P2_out, G1_out);
  and P2P1G0 (P2P1G0_out, P1_out, P2_out, G0_out);
  and G0 (G0_out, x[0], y[0]);
  and G1 (G1_out, x[1], y[1]);
  and G2 (G2_out, x[2], y[2]);
  and G3 (G3_out, x[3], y[3]);
  xor P0 (P0_out, x[0], y[0]);
  xor P1 (P1_out, x[1], y[1]);
  xor P2 (P2_out, x[2], y[2]);
  xor P3 (P3_out, x[3], y[3]);
  and and_1 (and_1_out, P0_out, C0);
  xor S1 (S0_out[1], P1_out, C1_out);
  and P1P0C0 (P1P0C0_out, P1_out, P0_out, C0);
  and P2P1P0C0 (P2P1P0C0_out, P2_out, P0_out, P1_out, C0);
  xor S3 (S0_out[3], P3_out, C3_out);
  and P3P2P1P0C0 (P3P2P1P0C0_out, P3_out, P2_out, P1_out, P0_out, C0);
  xor S0 (S0_out[0], P0_out, C0);
  or C1 (C1_out, G0_out, and_1_out);
  and P1G0 (P1G0_out, P1_out, G0_out);
  xor S2 (S0_out[2], P2_out, C2_out);
  or C3 (C3_out, G2_out, P2G1_out, P2P1G0_out, P2P1P0C0_out);
  and P3P2P1G0 (P3P2P1G0_out, P3_out, P2_out, P1_out, G0_out);
  and P3P2G1 (P3P2G1_out, P3_out, P2_out, G1_out);
  and P3G2 (P3G2_out, G2_out, P3_out);
  or C2 (C2_out, G1_out, P1G0_out, P1P0C0_out);
  or C4 (C4_out[0], G3_out, P3G2_out, P3P2G1_out, P3P2P1G0_out, P3P2P1P0C0_out);
  Hex_Digit_Display hex_digit_display_1 (.value({{3{in_4}}, C4_out[0]}));  // open: dp
  Hex_Digit_Display hex_digit_display_2 (.value(S0_out));  // open: dp
endmodule
