// Logisim project universalshiftregister.circ as structural Verilog: 1 circuit, main circuit main
module main (
  input  I0,
  input  I1,
  input  I2,
  input  I3,
  input  in_5,
  input  [1:0] selector_lines,
  output out_7,
  output out_8,
  output out_9,
  output out_10
);

  wire clock_1_out, multiplexer_1_out, multiplexer_2_out, multiplexer_3_out, multiplexer_4_out;

  Clock clock_1 (.out(clock_1_out));
  Multiplexer #(.select(2)) multiplexer_1 (
    .in0(in_5), .in1(out_9), .in2(I0), .in3(out_7), .out(multiplexer_1_out), .sel(selector_lines));
  D_Flip_Flop d_ff_1 (.D(multiplexer_1_out), .clk(clock_1_out), .Q(out_7));  // open: Qn, preset, reset
  Multiplexer #(.select(2)) multiplexer_2 (
    .in0(out_7), .in1(out_10), .in2(I1), .in3(out_9), .out(multiplexer_2_out), .sel(selector_lines));
  D_Flip_Flop d_ff_2 (.D(multiplexer_2_out), .clk(clock_1_out), .Q(out_9));  // open: Qn, preset, reset
  Multiplexer #(.select(2)) multiplexer_3 (
    .in0(out_9), .in1(out_8), .in2(I2), .in3(out_10), .out(multiplexer_3_out), .sel(selector_lines));
  D_Flip_Flop d_ff_3 (.D(multiplexer_3_out), .clk(clock_1_out), .Q(out_10));  // open: Qn, preset, reset
  Multiplexer #(.select(2)) multiplexer_4 (
    .in0(out_10), .in1(in_5), .in2(I3), .in3(out_8), .out(multiplexer_4_out), .sel(selector_lines));
  D_Flip_Flop d_ff_4 (.D(multiplexer_4_out), .clk(clock_1_out), .Q(out_8));  // open: Qn, preset, reset
endmodule
